# Fritzing sketch aula04 (saved by Fritzing 0.9.3b)
breadboards: 1

parts:
  R1 = Resistor [tolerance=±5% resistance=220 package=THT]
  S1 = Pushbutton [package="[THT]"]
  Part1 = Arduino Uno (Rev3)

nets:
  N1: R1.Pin_0, S1.Pin_1, S1.Pin_2, Part1.D7
  N2: R1.Pin_1, Part1.GND
  N3: S1.Pin_3, S1.Pin_4, Part1.5V
