# Fritzing sketch aula09 (saved by Fritzing 0.9.3b)
breadboards: 1

parts:
  Part1 = Arduino Uno (Rev3)
  R1 = Photocell (LDR) [package=THT]
  R2 = Resistor [tolerance=±5% resistance=220 package=THT]
  LED3 = LED - 5mm [color="Red (633nm)" package="5 mm [THT]"]

nets:
  N1: Part1.A0, R1.pin_1, R2.Pin_0
  N2: Part1.D7, LED3.anode
  N3: Part1.5V, R1.pin_0
  N4: R2.Pin_1, LED3.cathode
