# Fritzing sketch projeto_basico_ascender_led (saved by Fritzing 0.9.3b)
breadboards: 1

parts:
  Componente1 = Arduino Uno (Rev3)
  LED1 = LED - 5mm [color="Red (633nm)" package="5 mm [THT]"]

nets:
  N1: Componente1.D13/SCK, LED1.anode
  N2: Componente1.GND, LED1.cathode
