# Fritzing sketch semaforo_simples (saved by Fritzing 0.9.3b)
breadboards: 1

parts:
  Componente1 = Arduino Uno (Rev3)
  LED1 = LED - 5mm [color="Red (633nm)" package="5 mm [THT]"]
  LED2 = LED - 5mm [color="Yellow (595nm)" package="5 mm [THT]"]
  LED3 = LED - 5mm [color="Green (570nm)" package="5 mm [THT]"]
  R1 = Resistor [tolerance=±5% resistance=220 package=THT]
  R2 = Resistor [tolerance=±5% resistance=220 package=THT]
  R3 = Resistor [tolerance=±5% resistance=220 package=THT]

nets:
  N1: Componente1.D11_PWM/MOSI, R3.Pin_1
  N2: Componente1.D12/MISO, R2.Pin_1
  N3: Componente1.D13/SCK, R1.Pin_1
  N4: Componente1.GND, LED1.cathode, LED2.cathode, LED3.cathode
  N5: LED1.anode, R3.Pin_0
  N6: LED2.anode, R2.Pin_0
  N7: LED3.anode, R1.Pin_0
