# Fritzing sketch prototipacao_led_semaforo_2 (saved by Fritzing 0.9.3b)
breadboards: 1

parts:
  LED1 = LED - 5mm [color="Red (633nm)" package="5 mm [THT]"]
  LED2 = LED - 5mm [color="Yellow (595nm)" package="5 mm [THT]"]
  LED3 = LED - 5mm [color="Green (570nm)" package="5 mm [THT]"]
  LED4 = LED - 5mm [color="Red (633nm)" package="5 mm [THT]"]
  LED5 = LED - 5mm [color="Yellow (595nm)" package="5 mm [THT]"]
  LED6 = LED - 5mm [color="Green (570nm)" package="5 mm [THT]"]
  Componente1 = Arduino Uno (Rev3)

nets:
  N1: LED1.cathode, LED1.anode, LED2.cathode, LED2.anode
  N2: LED3.cathode, LED3.anode
  N3: LED4.cathode, LED4.anode, LED5.cathode, LED5.anode
  N4: LED6.cathode, LED6.anode
  N5: Componente1.D8, Componente1.D9_PWM, Componente1.D10_PWM/SS, Componente1.D11_PWM/MOSI, Componente1.D12/MISO, Componente1.D13/SCK, Componente1.GND
