# Fritzing sketch sensor]-ultrasonico (saved by Fritzing 0.9.3b)
breadboards: 1

parts:
  Componente1 = Arduino Uno (Rev3)
  HC-SR04_Sensor_1 = HC-SR04 Ultrasonic Distance Sensor

nets:
  N1: Componente1.D12/MISO, HC-SR04_Sensor_1.ECHO
  N2: Componente1.D13/SCK, HC-SR04_Sensor_1.TRIG
  GND: Componente1.GND, HC-SR04_Sensor_1.GND
  5V: Componente1.5V, HC-SR04_Sensor_1.VCC
