# Fritzing sketch sensor_de_obstaculo (saved by Fritzing 0.9.3b)
breadboards: 1

parts:
  Componente1 = Arduino Uno (Rev3)
  HC-SR04_Sensor_1 = HC-SR04 Ultrasonic Distance Sensor
  LED1 = LED - 5mm [color="Red (633nm)" package="5 mm [THT]"]
  J1 = Piezo Speaker

nets:
  N1: Componente1.D10_PWM/SS, J1.pin2
  N2: Componente1.D11_PWM/MOSI, LED1.anode
  N3: Componente1.D12/MISO, HC-SR04_Sensor_1.ECHO
  N4: Componente1.D13/SCK, HC-SR04_Sensor_1.TRIG
  GND: Componente1.GND, HC-SR04_Sensor_1.GND, LED1.cathode, J1.pin1
  5V: Componente1.5V, HC-SR04_Sensor_1.VCC
