# Fritzing sketch botaopressionado (saved by Fritzing 0.9.3b)
breadboards: 1

parts:
  Componente1 = Arduino Uno (Rev3)
  S1 = Momentary Switch [package=ksa_sealed_tac_switch]
  R1 = Resistor [tolerance=±5% resistance=220 package="2512 [SMD]"]

nets:
  N1: Componente1.D2, R1.Pin_0
  N2: Componente1.GND, S1.2
  N3: S1.4, R1.Pin_1

// code stored in the sketch: botaopressionado.ino
int botao = 2;
int leituraBotao=0;

void setup() {
  pinMode(botao, INPUT);
  Serial.begin(10000);
  digitalWrite(botao, 1);
}

void loop() {
  
  leituraBotao = digitalRead(botao);

  if (leituraBotao == 0){
    
    Serial.println("ativado");
    
  }else{
    
    Serial.println("desativado");
    
  }
}
