# Fritzing sketch ldrcomled (saved by Fritzing 0.9.3b)
breadboards: 1

parts:
  Componente1 = Arduino Uno (Rev3) - ICSP
  LED1 = smd LED [color="Red (633nm)" package="0805 [SMD]"]
  R1 = Photocell (LDR) [package=THT]
  R2 = Resistor [tolerance=±5% resistance=220 package="0603 [SMD]"]
  R3 = Resistor [tolerance=±5% resistance=220 package="1206 [SMD]"]

nets:
  N1: Componente1.A0, R1.pin_0, R2.Pin_1
  N2: Componente1.D13/SCK, LED1.anode
  N3: Componente1.5V, R1.pin_1
  N4: Componente1.GND, R2.Pin_0, R3.Pin_0
  N5: LED1.cathode, R3.Pin_1

// code stored in the sketch: ldrcomled.ino
const int ledPin = 13;
const int ldrPin = A0;

void setup()
{
  Serial.begin(9600);
  pinMode(ledPin, OUTPUT);
  pinMode(ldrPin, INPUT);
}

void loop()
{
  int ldrSt = analogRead(ldrPin);
  if(ldrSt >301)
  {
    digitalWrite(ledPin, HIGH);
  }
  else
  {
    digitalWrite(ledPin, LOW);
  }
}
