# Fritzing sketch led1semafaro (saved by Fritzing 0.9.3b)
breadboards: 1

parts:
  Componente1 = Arduino Uno (Rev3)
  LED1 = LED - 5mm [color="Red (633nm)" package="5 mm [THT]"]
  LED2 = LED - 5mm [color="Yellow (595nm)" package="5 mm [THT]"]
  LED3 = LED - 5mm [color="Green (565nm)" package="5 mm [THT]"]
  R1 = Resistor [tolerance=±5% resistance=220 package=THT]
  R2 = Resistor [tolerance=±5% resistance=220 package=THT]
  R3 = Resistor [tolerance=±5% resistance=220 package=THT]

nets:
  N1: Componente1.D2, R2.Pin_0
  N2: Componente1.D3_PWM, R3.Pin_0
  N3: Componente1.D4, R1.Pin_0
  N4: Componente1.GND, LED1.cathode, LED2.cathode, LED3.cathode
  N5: LED1.anode, R2.Pin_1
  N6: LED2.anode, R3.Pin_1
  N7: LED3.anode, R1.Pin_1

// code stored in the sketch: exercicio01.ino
void setup() {

pinMode(2,OUTPUT);//vermelho
pinMode(3,OUTPUT);//amarelo
pinMode(4,OUTPUT);//verde

}

void loop() {

digitalWrite(2, HIGH);
delay(5000);
digitalWrite(2, LOW);
digitalWrite(4, HIGH);
delay(5000);
digitalWrite(4, LOW);
digitalWrite(3, HIGH);
delay(2000);
digitalWrite(3, LOW);
}
