# Fritzing sketch led3semafaro (saved by Fritzing 0.9.3b)
breadboards: 1

parts:
  Componente1 = Arduino Uno (Rev3)
  LED1 = smd LED [color="Red (633nm)" package="0603 [SMD]"]
  LED2 = smd LED [color="Yellow (595nm)" package="0603 [SMD]"]
  LED3 = smd LED [color="Green (555nm)" package="0603 [SMD]"]
  LED4 = smd LED [color="Red (633nm)" package="0603 [SMD]"]
  LED5 = smd LED [color="Yellow (595nm)" package="0603 [SMD]"]
  LED6 = smd LED [color="Green (555nm)" package="0603 [SMD]"]
  LED7 = smd LED [color="Red (633nm)" package="0603 [SMD]"]
  LED8 = smd LED [color="Yellow (595nm)" package="0603 [SMD]"]
  LED9 = smd LED [color="Green (555nm)" package="0603 [SMD]"]

nets:
  N1: Componente1.D8, LED7.anode
  N2: Componente1.D9_PWM, LED8.anode
  N3: Componente1.D10_PWM/SS, LED9.anode
  N4: Componente1.GND, LED1.cathode, LED2.cathode, LED3.cathode, LED4.cathode, LED5.cathode, LED6.cathode, LED7.cathode, LED8.cathode, LED9.cathode
  N5: Componente1.D2, LED1.anode
  N6: Componente1.D3_PWM, LED2.anode
  N7: Componente1.D4, LED3.anode
  N8: Componente1.D5_PWM, LED4.anode
  N9: Componente1.D6_PWM, LED5.anode
  N10: Componente1.D7, LED6.anode

// code stored in the sketch: exercicio02.ino
void setup() {

pinMode(2,OUTPUT);
pinMode(3,OUTPUT);
pinMode(4,OUTPUT);
pinMode(5,OUTPUT);
pinMode(6,OUTPUT);
pinMode(7,OUTPUT);
pinMode(8,OUTPUT);
pinMode(9,OUTPUT);
pinMode(10,OUTPUT);

}

void loop() {

digitalWrite(2, HIGH);
digitalWrite(7, HIGH);//
digitalWrite(10, HIGH);//
delay(2000);
digitalWrite(7, LOW);//
digitalWrite(10, LOW);//
digitalWrite(6, HIGH);//
digitalWrite(9, HIGH);//
delay(1000);
digitalWrite(2, LOW);
digitalWrite(6, LOW);//
digitalWrite(9, LOW);//
digitalWrite(5, HIGH);//
digitalWrite(8, HIGH);//
digitalWrite(4, HIGH);
delay(2000);
digitalWrite(3, HIGH);
digitalWrite(4, LOW);
delay(1000);
digitalWrite(3, LOW);
digitalWrite(5, LOW);//
digitalWrite(8, LOW);//


}
