# Fritzing sketch ledbotaopress (saved by Fritzing 0.9.3b)
breadboards: 1

parts:
  Componente1 = Arduino Uno (Rev3)
  R1 = Resistor [tolerance=±5% resistance=220 package=THT]
  S1 = Pushbutton [package="[THT]"]
  LED1 = smd LED [color="Red (633nm)" package="0805 [SMD]"]

nets:
  N1: Componente1.GND, LED1.cathode
  N2: Componente1.D2, R1.Pin_1
  N3: R1.Pin_0, S1.Pin_1, S1.Pin_2
  N4: S1.Pin_3, LED1.anode

// code stored in the sketch: ledbotaopress.ino
void setup()
{
  pinMode(2, OUTPUT);
}

void loop()
{
  digitalWrite(2, HIGH);
}
