# Fritzing sketch sensorcapacitancia (saved by Fritzing 0.9.3b)
breadboards: 1

parts:
  Componente1 = Arduino Uno (Rev3)
  R1 = Resistor [tolerance=±5% resistance=220 package="2512 [SMD]"]
  LED1 = LED - 5mm [color="White (6500K)" package="5 mm [THT]"]

nets:
  N1: Componente1.D13/SCK, LED1.cathode
  N2: Componente1.GND, R1.Pin_0
  N3: R1.Pin_1, LED1.anode

notes:
  "Alumínio condutor"
