# Fritzing sketch sensorestaciona (saved by Fritzing 0.9.3b)
breadboards: 1

parts:
  hc-sr1 = hc-sr04
  LED1 = smd LED [color="Blue (430nm)" package="0603 [SMD]"]
  Componente1 = Arduino Uno (Rev3) - ICSP
  J1 = Piezo Speaker
  R1 = Resistor [tolerance=±5% resistance=220 package=THT]

nets:
  VCC: hc-sr1.VCC, Componente1.5V
  N1: hc-sr1.Trig, Componente1.D9_PWM
  N2: hc-sr1.Echo, Componente1.D10_PWM/SS
  GND: hc-sr1.GND, LED1.cathode, Componente1.GND, J1.pin2
  N3: LED1.anode, R1.Pin_0
  N4: Componente1.D11_PWM/MOSI, J1.pin1
  N5: Componente1.D13/SCK, R1.Pin_1

// code stored in the sketch: sensorestaciona.ino
const int trigPin = 9;
const int echoPin = 10;
const int buzzer = 11;
const int ledPin = 13;

long duration;
int distance;
int safetyDistance;

void setup()
{
  pinMode(trigPin, OUTPUT);
  pinMode(echoPin, INPUT);
  pinMode(buzzer, OUTPUT);
  pinMode(ledPin, OUTPUT);
  Serial.begin(9600);
}

void loop()
{
  digitalWrite(trigPin, LOW);
  delayMicroseconds(2);
  digitalWrite(trigPin, HIGH);
  delayMicroseconds(1);
  digitalWrite(trigPin, LOW);
  
  duration = pulseIn(echoPin, HIGH);
  distance = duration * 0.034/2;
  safetyDistance = distance;
  
  if(safetyDistance <6)
  {
    digitalWrite(buzzer, HIGH);
    digitalWrite(ledPin, HIGH);
  }
  else
  {
    digitalWrite(buzzer, LOW);
    digitalWrite(ledPin, LOW);
  }
  Serial.print("\ndistancia em cm: ");
  Serial.print(distance);
  delay(100);
}
