# Fritzing sketch sirenepolicial (saved by Fritzing 0.9.3b)
breadboards: 1

parts:
  J1 = Piezo Speaker
  Componente1 = Arduino Uno (Rev3) - ICSP

nets:
  N1: J1.pin1, Componente1.GND
  N2: J1.pin2, Componente1.D10_PWM/SS

// code stored in the sketch: sirenepolicial.ino
int tempo= 10;
int frequencia = 0;
int Pinofalante = 10;
void setup()
{
  pinMode(Pinofalante,OUTPUT);
}
void loop()
{
  for (frequencia = 150; frequencia < 1800; frequencia += 1) 
  {
    tone(Pinofalante, frequencia, tempo); 
    delay(1);
  }
  for (frequencia = 1800; frequencia > 150; frequencia -= 1) 
  {
    tone(Pinofalante, frequencia, tempo); 
    delay(1);
  }
}
