# Fritzing sketch ultramedirdist (saved by Fritzing 0.9.3b)

parts:
  Componente1 = Arduino Uno (Rev3) - ICSP
  hc-sr1 = hc-sr04

nets:
  N1: Componente1.D9_PWM, hc-sr1.Echo
  N2: Componente1.D10_PWM/SS, hc-sr1.Trig
  5V: Componente1.5V, hc-sr1.VCC
  GND: Componente1.GND, hc-sr1.GND

// code stored in the sketch: ultramedirdist.ino
const byte trigger_Pin = 9;
const byte echo_Pin = 10;

unsigned long duration;
unsigned int distance;

void setup()
{
  Serial.begin(9600);
  pinMode(echo_Pin, INPUT);
  pinMode(trigger_Pin, OUTPUT);
}

void loop()
{
  digitalWrite(trigger_Pin, LOW);
  delay(1);
  digitalWrite(trigger_Pin, HIGH);
  delayMicroseconds(10);
  digitalWrite(trigger_Pin, LOW);
  
  duration = pulseIn(echo_Pin, HIGH);
  distance = duration * 0.017;
  
  Serial.print("\ndistancia em cm: ");
  Serial.print(distance);
  delay(100);
}
