# Fritzing sketch 7 - botão-com-LED (saved by Fritzing 0.9.2b)
breadboards: 1

parts:
  Componente1 = Arduino Uno (Rev3)
  S1 = Pushbutton [package="[THT]"]
  R1 = Resistor [tolerance=±5% resistance=220 package=THT]
  LED1 = LED - 5mm [color="Red (633nm)" package="5 mm [THT]"]

nets:
  N1: Componente1.A0, R1.Pin_0
  N2: Componente1.D13/SCK, LED1.anode
  N3: Componente1.GND, S1.Pin_1, S1.Pin_2, LED1.cathode
  N4: S1.Pin_3, S1.Pin_4, R1.Pin_1
