# Fritzing sketch aula08 (saved by Fritzing 0.9.3b)
breadboards: 1

parts:
  hc-sr1 = hc-sr04
  J1 = Piezo Speaker
  Part1 = Arduino Uno (Rev3)

nets:
  N1: hc-sr1.GND, J1.pin1
  N2: J1.pin2, Part1.D13/SCK
