# Fritzing sketch 10 - sirene-policial (saved by Fritzing 0.9.2b)
breadboards: 1

parts:
  Componente1 = Arduino Uno (Rev3)
  J1 = Piezo Speaker

nets:
  N1: Componente1.D12/MISO, J1.pin2
  N2: Componente1.GND, J1.pin1
