# Fritzing sketch 14 - Relé-com-LDR (saved by Fritzing 0.9.2b)
breadboards: 1

parts:
  R1 = Photocell (LDR) [package=THT]
  Componente1 = Arduino Uno (Rev3)
  R2 = Resistor [tolerance=±5% resistance=220 package="0402 [SMD]"]

nets:
  N1: R1.pin_1, Componente1.A5/SCL, R2.Pin_0
  N2: Componente1.GND, R2.Pin_1

notes:
  RELÉ
