# Fritzing sketch Acender_LEDs_em_sequ_ncia (saved by Fritzing 0.9.2b)
breadboards: 1

parts:
  Componente1 = Arduino Uno (Rev3)
  LED1 = LED - 5mm [color="Red (633nm)" package="5 mm [THT]"]
  LED2 = LED - 5mm [color="Yellow (595nm)" package="5 mm [THT]"]
  LED3 = LED - 5mm [color="Green (570nm)" package="5 mm [THT]"]
  LED4 = LED - 5mm [color="White (4500K)" package="5 mm [THT]"]
  LED5 = LED - 5mm [color="Blue (525nm)" package="5 mm [THT]"]

nets:
  N1: Componente1.D9_PWM, LED5.anode
  N2: Componente1.D10_PWM/SS, LED4.anode
  N3: Componente1.D11_PWM/MOSI, LED3.anode
  N4: Componente1.D12/MISO, LED2.anode
  N5: Componente1.D13/SCK, LED1.anode
  N6: Componente1.GND, LED1.cathode, LED2.cathode, LED3.cathode, LED4.cathode, LED5.cathode
