# Fritzing sketch 13 - LDR-com-LED (saved by Fritzing 0.9.2b)
breadboards: 1

parts:
  R1 = Photocell (LDR) [package=THT]
  LED1 = smd LED [color="Red (633nm)" package="0603 [SMD]"]
  Componente1 = Arduino Uno (Rev3)
  R2 = Resistor [tolerance=±5% resistance=220 package="0402 [SMD]"]

nets:
  N1: R1.pin_0, Componente1.5V
  N2: R1.pin_1, Componente1.A5/SCL, R2.Pin_0
  N3: LED1.cathode, Componente1.GND, R2.Pin_1
  N4: LED1.anode, Componente1.D10_PWM/SS
